# Fritzing sketch Sketch_blink_led (saved by Fritzing 0.9.3b)
breadboards: 1

parts:
  Arduino_Uno = Arduino Uno (Rev3)
  Raspberry_Pi = Raspberry Pi 3 [part_number=RPI-3-V1.2]  # not connected
  R = Resistor [tolerance=±5% resistance=100 package=THT]
  LED1 = LED - 5mm [color="Red (633nm)" package="5 mm [THT]"]

nets:
  N1: Arduino_Uno.D13/SCK, LED1.anode
  N2: Arduino_Uno.GND, R.Pin_0
  N3: R.Pin_1, LED1.cathode
