# Fritzing sketch Sketch_7-Segment (saved by Fritzing 0.9.3b)
breadboards: 1

parts:
  Arduino_Uno = Arduino Uno (Rev3)
  Raspberry_Pi = Raspberry Pi 3 [part_number=RPI-3-V1.2]  # not connected
  R1 = Resistor [tolerance=±5% resistance=220 package=THT]
  R2 = Resistor [tolerance=±5% resistance=220 package=THT]
  R3 = Resistor [tolerance=±5% resistance=220 package=THT]
  R4 = Resistor [tolerance=±5% resistance=220 package=THT]
  7_Segment1 = 7 Segment Display
  R5 = Resistor [tolerance=±5% resistance=220 package=THT]
  R6 = Resistor [tolerance=±5% resistance=220 package=THT]
  R7 = Resistor [tolerance=±5% resistance=220 package=THT]

nets:
  N1: Arduino_Uno.D8, R3.Pin_1
  N2: Arduino_Uno.D2, R4.Pin_1
  N3: Arduino_Uno.D3_PWM, R2.Pin_1
  N4: Arduino_Uno.D4, R1.Pin_0, R1.Pin_1, 7_Segment1.Segment_B
  N5: Arduino_Uno.D5_PWM, 7_Segment1.Segment_C, R7.Pin_0, R7.Pin_1
  N6: Arduino_Uno.D6_PWM, 7_Segment1.Segment_DP, R6.Pin_0, R6.Pin_1
  N7: Arduino_Uno.D7, R5.Pin_1
  N8: Arduino_Uno.GND, 7_Segment1.common_anode
  N9: R2.Pin_0, 7_Segment1.Segment_G
  N10: R3.Pin_0, 7_Segment1.Segment_E
  N11: R4.Pin_0, 7_Segment1.Segment_F
  N12: 7_Segment1.Segment_D, R5.Pin_0
