# Fritzing sketch Sketch_CdS (saved by Fritzing 0.9.3b)
breadboards: 1

parts:
  Arduino_Uno = Arduino Uno (Rev3)
  Raspberry_Pi = Raspberry Pi 3 [part_number=RPI-3-V1.2]  # not connected
  R1 = Resistor [tolerance=±5% resistance=220 package=THT]  # not connected
  LED1 = LED - 5mm [color="Red (633nm)" package="5 mm [THT]"]
  R2 = Photocell (LDR) [package=THT]
  R3 = Resistor [tolerance=±5% resistance=220 package=THT]

nets:
  N1: Arduino_Uno.A0, R2.pin_1, R3.Pin_0
  N2: Arduino_Uno.D11_PWM/MOSI, LED1.cathode
  N3: Arduino_Uno.5V, R3.Pin_1
  N4: Arduino_Uno.GND, R2.pin_0
