# Fritzing sketch Sketch_infrared_sensor (saved by Fritzing 0.9.3b)
breadboards: 1

parts:
  Arduino_Uno = Arduino Uno (Rev3)
  Raspberry_Pi = Raspberry Pi 3 [part_number=RPI-3-V1.2]  # not connected
  LED1 = LED - 5mm [color="Red (633nm)" package="5 mm [THT]"]
  R1 = Resistor [tolerance=±5% resistance=220 package=THT]
  J1 = Infrared Proximity Sensor

nets:
  N1: Arduino_Uno.A0, J1.Vout
  N2: Arduino_Uno.D13/SCK, R1.Pin_1
  5V: Arduino_Uno.5V, J1.Vcc
  GND: Arduino_Uno.GND, LED1.cathode, J1.GND
  N3: LED1.anode, R1.Pin_0
