# Fritzing sketch Sketch_RGB_led (saved by Fritzing 0.9.3b)
breadboards: 1

parts:
  Arduino_Uno = Arduino Uno (Rev3)
  Raspberry_Pi = Raspberry Pi 3 [part_number=RPI-3-V1.2]  # not connected
  R1 = Resistor [tolerance=±5% resistance=220 package=THT]
  LED2 = RGB LED (com. cathode, rgb) [package="5 mm [THT]"]
  R2 = Resistor [tolerance=±5% resistance=220 package=THT]
  R3 = Resistor [tolerance=±5% resistance=220 package=THT]

nets:
  N1: Arduino_Uno.D9_PWM, R2.Pin_1
  N2: Arduino_Uno.D10_PWM/SS, R1.Pin_1
  N3: Arduino_Uno.D11_PWM/MOSI, R3.Pin_1
  N4: Arduino_Uno.GND, LED2.red_anode
  N5: R1.Pin_0, LED2.green_anode
  N6: LED2.common_cathode, R3.Pin_0
  N7: LED2.blue_anode, R2.Pin_0
