# Fritzing sketch Sketch_buzzer (saved by Fritzing 0.9.3b)
breadboards: 1

parts:
  Arduino_Uno = Arduino Uno (Rev3)
  Raspberry_Pi = Raspberry Pi 3 [part_number=RPI-3-V1.2]  # not connected
  J1 = Piezo Speaker
  R1 = Resistor [tolerance=±5% resistance=220 package=THT]  # not connected

nets:
  N1: Arduino_Uno.GND, J1.pin1
