# Fritzing sketch Sketch__ductswitch (saved by Fritzing 0.9.3b)
breadboards: 1

parts:
  Arduino_Uno = Arduino Uno (Rev3)
  Raspberry_Pi = Raspberry Pi 3 [part_number=RPI-3-V1.2]  # not connected
  R = Resistor [tolerance=±5% resistance=100 package=THT]
  LED1 = LED - 5mm [color="Red (633nm)" package="5 mm [THT]"]
  R1 = Resistor [tolerance=±5% resistance=220 package=THT]
  S1 = Pushbutton [package="[THT]"]

nets:
  N1: Arduino_Uno.D13/SCK, LED1.anode
  N2: Arduino_Uno.D7, R1.Pin_0, S1.Pin_1, S1.Pin_2
  N3: Arduino_Uno.GND, R.Pin_0, R1.Pin_1, S1.Pin_3, S1.Pin_4
  N4: R.Pin_1, LED1.cathode
