# Fritzing sketch Sketch_pressure_sensor (saved by Fritzing 0.9.3b)
breadboards: 1

parts:
  Arduino_Uno = Arduino Uno (Rev3)
  Raspberry_Pi = Raspberry Pi 3 [part_number=RPI-3-V1.2]  # not connected
  R1 = Resistor [tolerance=±5% resistance=220 package=THT]  # not connected
  LED1 = LED - 5mm [color="Red (633nm)" package="5 mm [THT]"]
  J1 = Basic Force Sensing Resistor (FSR) [package=THT]
  R2 = Resistor [tolerance=±5% resistance=220 package=THT]

nets:
  N1: Arduino_Uno.A0, J1.pin_1, R2.Pin_0
  N2: Arduino_Uno.D11_PWM/MOSI, LED1.cathode
  N3: Arduino_Uno.5V, R2.Pin_1
  N4: Arduino_Uno.GND, J1.pin_0
