# Fritzing sketch Sketch_servo (saved by Fritzing 0.9.3b)
breadboards: 1

parts:
  Arduino_Uno = Arduino Uno (Rev3)
  Raspberry_Pi = Raspberry Pi 3 [part_number=RPI-3-V1.2]  # not connected
  J1 = Basic Servo

nets:
  N1: Arduino_Uno.D11_PWM/MOSI, J1.pulse
  5V: Arduino_Uno.5V, J1.vcc
  GND: Arduino_Uno.GND, J1.gnd
