# Fritzing sketch Sketch_variable_resistor (saved by Fritzing 0.9.3b)
breadboards: 1

parts:
  Arduino_Uno = Arduino Uno (Rev3)
  Raspberry_Pi = Raspberry Pi 3 [part_number=RPI-3-V1.2]  # not connected
  R1 = Resistor [tolerance=±5% resistance=220 package=THT]  # not connected
  LED1 = LED - 5mm [color="Red (633nm)" package="5 mm [THT]"]
  R4 = Rotary Potentiometer (Small) [maximum_resistance=100kΩ package=THT]

nets:
  N1: Arduino_Uno.A0, R4.wiper
  N2: Arduino_Uno.D11_PWM/MOSI, LED1.cathode
  N3: Arduino_Uno.5V, R4.leg2
  N4: Arduino_Uno.GND, R4.leg1
